// Logisim project 6502.circ as structural Verilog: 2 circuits, main circuit main
module main (
);

  wire and_1_out, and_2_out, and_3_out, and_4_out, button_1_out, button_2_out, clock_1_out, nand_1_out,
       nand_2_out, not_1_out, not_2_out, not_3_out, not_4_out, pull_resistor_1_node, w65c02s_pdip_40_1_p1,
       w65c02s_pdip_40_1_p10;
  wire [3:1] w65c22_1_p6;
  wire [7:0] controlled_buffer_2_out, ram_1_dout, rom_1_data, w65c02s_pdip_40_1_p11, w65c22_1_p1,
       w65c22_1_p9, w65c22_1_p10, w65c22_1_p12;
  wire [8:8] undriven;
  wire [11:0] w65c22_1_p2;

  Pull_Resistor #(.pull(1)) pull_resistor_1 (.node(pull_resistor_1_node));
  Clock clock_1 (.out(clock_1_out));
  Button #(.press("passive")) button_1 (.out(button_1_out));
  // W65C02S__PDIP_40 w65c02s_pdip_40_1: pin names not known; wires that end beside it: w65c02s_pdip_40_1_p1, 1'b1, pull_resistor_1_node, 1'b1, 1'b1, button_1_out, 1'b1, clock_1_out, 1'b1, w65c02s_pdip_40_1_p10, w65c02s_pdip_40_1_p11[0], w65c02s_pdip_40_1_p11[1], w65c02s_pdip_40_1_p11[2], w65c02s_pdip_40_1_p11[3], w65c02s_pdip_40_1_p11[4], w65c02s_pdip_40_1_p11[5], w65c02s_pdip_40_1_p11[6], w65c02s_pdip_40_1_p11[7], 1'b0
  nand nand_1 (nand_1_out, w65c22_1_p6[3], w65c22_1_p6[3]);
  // Probe on w65c02s_pdip_40_1_p11
  nand nand_2 (nand_2_out, w65c22_1_p6[2], nand_1_out);
  // Probe on {w65c22_1_p6[2:1], undriven[8], w65c22_1_p2}
  ROM #(.addrWidth(15)) rom_1 (.addr({w65c22_1_p6[2:1], undriven[8], w65c22_1_p2}), .data(rom_1_data));
  not not_1 (not_1_out, nand_2_out);
  and and_1 (and_1_out, not_1_out, w65c22_1_p6[1]);
  Button #(.press("passive")) button_2 (.out(button_2_out));
  LED RO (.in(w65c22_1_p6[3]));
  // Probe on w65c02s_pdip_40_1_p11
  assign w65c02s_pdip_40_1_p11 = w65c22_1_p6[3] ? rom_1_data : 8'bz;  // Controlled_Buffer controlled_buffer_1
  // Probe on rom_1_data
  // W65C22 w65c22_1: pin names not known; wires that end beside it: w65c22_1_p1, w65c22_1_p2[3:0], w65c02s_pdip_40_1_p11, clock_1_out, button_1_out, w65c22_1_p6[1], nand_2_out, w65c02s_pdip_40_1_p10, w65c22_1_p9, w65c22_1_p10, w65c02s_pdip_40_1_p11, w65c22_1_p12, button_2_out, w65c02s_pdip_40_1_p1
  and and_2 (and_2_out, and_3_out, not_2_out);
  assign controlled_buffer_2_out = and_2_out ? w65c02s_pdip_40_1_p11 : 8'bz;  // Controlled_Buffer controlled_buffer_2
  not not_2 (not_2_out, w65c02s_pdip_40_1_p10);
  // Probe on controlled_buffer_2_out
  RAM #(.addrWidth(15)) ram_1 (
    .addr({w65c22_1_p6[2:1], undriven[8], w65c22_1_p2}), .we(not_2_out), .oe(w65c02s_pdip_40_1_p10),
    .clk(clock_1_out), .din(controlled_buffer_2_out), .dout(ram_1_dout));
  // Probe on {w65c22_1_p6[2:1], undriven[8], w65c22_1_p2}
  and and_3 (and_3_out, not_4_out, not_3_out);
  not not_3 (not_3_out, w65c22_1_p6[2]);
  not not_4 (not_4_out, w65c22_1_p6[3]);
  LED RA (.in(and_3_out));
  LED R (.in(w65c02s_pdip_40_1_p10));
  // Probe on w65c02s_pdip_40_1_p11
  // Probe on w65c02s_pdip_40_1_p11
  // Probe on w65c22_1_p10
  // Probe on w65c22_1_p12
  LED W (.in(not_2_out));
  assign w65c02s_pdip_40_1_p11 = and_4_out ? ram_1_dout : 8'bz;  // Controlled_Buffer controlled_buffer_3
  and and_4 (and_4_out, and_3_out, w65c02s_pdip_40_1_p10);
  // Probe on {w65c22_1_p6, undriven[8], w65c22_1_p2}
  LED IO (.in(and_1_out));
  // Probe on w65c02s_pdip_40_1_p11
  // Probe on ram_1_dout

  // Notes on the sheet:
  //   contents of rom_1 (hex, n*v repeats v):
  //   a2 ff 9a 58 a9 82 8d e 60 a9 0 8d c 60 a9 ff 8d 2 60 a9 e0 8d 3 60 a9 0 8d a 2 8d b 2 4c 20 80 48 8a
  //   48 98 48 ee a 2 d0 3 ee b 2 a2 ff a0 ff ca d0 fd 88 d0 fa 2c 1 60 68 a8 68 aa 68 40 32695*0 23 80 0
  //   80 23 80
endmodule

module RAMTEST (
);

  wire button_1_out, clock_1_out, not_1_out, or_1_out, or_2_out;
  wire [6:0] counter_1_q, ram_1_dout;

  Clock clock_1 (.out(clock_1_out));
  or or_1 (or_1_out, clock_1_out, button_1_out);
  Counter #(.max('h7f), .width(7)) counter_1 (
    .clr(button_1_out), .clk(or_1_out), .Q(counter_1_q));  // open: load, up, count, D, carry
  // Probe on counter_1_q
  not not_1 (not_1_out, clock_1_out);
  RAM #(.addrWidth(7), .dataWidth(7)) ram_1 (
    .addr(counter_1_q), .we(clock_1_out), .oe(not_1_out), .clk(clock_1_out), .din(counter_1_q),
    .dout(ram_1_dout));
  // Probe on ram_1_dout
  or or_2 (or_2_out, not_1_out, button_1_out);
  TTY tty_1 (.data(ram_1_dout), .clk(or_2_out), .clr(button_1_out));  // open: we
  Button button_1 (.out(button_1_out));
endmodule
